# Fritzing sketch arduino-wheel-robot-diagram (saved by Fritzing 0.9.7b)
breadboards: 1

parts:
  Arduino2 = Arduino Mega 2560 (Rev3)
  M3 = DC Motor
  M8 = BTS7960
  U2 = LIPO-1000mAh [package=lipo-1000]
  M9 = BTS7960
  M10 = DC Motor
  M11 = BTS7960
  M12 = DC Motor
  M13 = BTS7960
  M14 = DC Motor

nets:
  N1: Arduino2.5V, M8.pin11, U2.+, M9.pin11, M11.pin11
  N2: Arduino2.GND, M8.pin12, U2.-, M9.pin12, M11.pin12
  N3: M3.pin_1, M8.pin10
  N4: M3.pin_2, M8.pin9
  N5: M9.pin9, M10.pin_2
  N6: M9.pin10, M10.pin_1
  N7: M11.pin9, M12.pin_2
  N8: M11.pin10, M12.pin_1
  N9: M13.pin9, M14.pin_2
  N10: M13.pin10, M14.pin_1

notes:
  11.1V
  3500 mAh

custom parts:
  BTS7960: BTS7960 43A Peak Power H-Bridge PWM Motor Driver
